// Logisim project RockPapSci.circ as structural Verilog: 1 circuit, main circuit main
module main (
  input  rock,
  input  paper,
  input  scissors,
  input  scissors_2,
  input  paper_2,
  input  rock_2
);

  wire transistor_1_out, transistor_2_out, transistor_3_out, transistor_4_out, transistor_5_out,
       transistor_6_out, transistor_7_out, transistor_9_out;

  LED led_1 (.in(transistor_7_out));
  LED led_2 (.in(transistor_9_out));
  Transistor #(.\type ("n")) transistor_1 (.in(1'b1), .out(transistor_1_out), .gate(scissors));
  Transistor #(.\type ("n")) transistor_2 (.in(1'b1), .out(transistor_2_out), .gate(paper));
  Transistor #(.\type ("n")) transistor_3 (.in(1'b1), .out(transistor_3_out), .gate(rock));
  Transistor #(.\type ("n"), .gate("br")) transistor_4 (.in(1'b1), .out(transistor_4_out), .gate(scissors_2));
  Transistor #(.\type ("n"), .gate("br")) transistor_5 (.in(1'b1), .out(transistor_5_out), .gate(paper_2));
  Transistor #(.\type ("n"), .gate("br")) transistor_6 (.in(1'b1), .out(transistor_6_out), .gate(rock_2));
  Transistor #(.\type ("n"), .gate("br")) transistor_7 (
    .in(transistor_2_out), .out(transistor_7_out), .gate(transistor_6_out));
  Transistor #(.\type ("n"), .gate("br")) transistor_8 (
    .in(transistor_3_out), .out(transistor_7_out), .gate(transistor_4_out));
  Transistor #(.\type ("n")) transistor_9 (.in(transistor_5_out), .out(transistor_9_out), .gate(transistor_3_out));
  Transistor #(.\type ("n"), .gate("br")) transistor_10 (
    .in(transistor_1_out), .out(transistor_7_out), .gate(transistor_5_out));
  Transistor #(.\type ("n")) transistor_11 (.in(transistor_6_out), .out(transistor_9_out), .gate(transistor_1_out));
  Transistor #(.\type ("n")) transistor_12 (.in(transistor_4_out), .out(transistor_9_out), .gate(transistor_2_out));

  // Notes on the sheet:
  //   Player 1
  //   Player 2
  //   Won?
  //   Won?
  //   -----------------------------------------------------------------
endmodule
