// Logisim project combinatorial.circ as structural Verilog: 3 circuits, main circuit main
module main (
  input  leap,
  input  month,
  input  in_3,
  input  in_4,
  input  in_5,
  input  in_6,
  input  day,
  input  in_8,
  input  in_9,
  input  in_10
);

  wire monthmax_1_numdays1, monthmax_1_numdays2, n2bit_less_or_eq_1_out, not_1_out, not_2_out, not_3_out,
       or_1_out, or_2_out;

  monthmax monthmax_1 (
    .month1(month), .numdays1(monthmax_1_numdays1), .month2(in_3), .month3(in_4), .month4(in_5),
    .leapyear(leap), .numdays2(monthmax_1_numdays2));
  LED led_1 (.in(or_1_out));
  _2bit_less_or_eq u_2bit_less_or_eq_1 (
    .bit1_1(in_9), .bit1_2(in_10), .bit2_1(monthmax_1_numdays1), .bit2_2(monthmax_1_numdays2),
    .out(n2bit_less_or_eq_1_out));
  or or_1 (or_1_out, n2bit_less_or_eq_1_out, or_2_out);
  or or_2 (or_2_out, not_3_out, not_2_out, not_1_out);
  not not_1 (not_1_out, in_6);
  not not_2 (not_2_out, day);
  not not_3 (not_3_out, in_8);

  // Notes on the sheet:
  //   Valid?
endmodule

module monthmax (
  input  month1,
  input  month2,
  input  month3,
  input  month4,
  input  leapyear,
  output numdays1,
  output numdays2
);

  wire and_1_out, and_2_out, and_3_out, and_4_out, and_5_out, not_1_out, not_2_out, not_3_out, not_4_out,
       not_5_out, not_6_out, not_7_out;

  not not_1 (not_1_out, month4);
  not not_2 (not_2_out, month1);
  not not_3 (not_3_out, month4);
  not not_4 (not_4_out, month1);
  not not_5 (not_5_out, month2);
  not not_6 (not_6_out, month3);
  not not_7 (not_7_out, month4);
  or or_1 (numdays1, not_1_out, month3, month2, month1);
  and and_1 (and_1_out, not_2_out, not_3_out);
  and and_2 (and_2_out, not_4_out, not_5_out, not_6_out, leapyear);
  and and_3 (and_3_out, month2, not_7_out);
  and and_4 (and_4_out, month2, month3);
  and and_5 (and_5_out, month1, month4);
  or or_2 (numdays2, and_1_out, and_2_out, and_3_out, and_4_out, and_5_out);
endmodule

module _2bit_less_or_eq (
  input  bit1_1,
  input  bit1_2,
  input  bit2_1,
  input  bit2_2,
  output out
);

  wire and_1_out, and_2_out, and_3_out, and_4_out, and_5_out, not_1_out, not_2_out, not_3_out, not_4_out,
       not_5_out;

  not not_1 (not_1_out, bit1_1);
  and and_1 (and_1_out, not_1_out, not_2_out);
  not not_2 (not_2_out, bit1_2);
  not not_3 (not_3_out, bit1_1);
  and and_2 (and_2_out, not_3_out, bit2_2);
  not not_4 (not_4_out, bit1_1);
  and and_3 (and_3_out, not_4_out, bit2_1);
  not not_5 (not_5_out, bit1_2);
  and and_4 (and_4_out, not_5_out, bit2_1);
  and and_5 (and_5_out, bit2_1, bit2_2);
  or or_1 (out, and_1_out, and_2_out, and_3_out, and_4_out, and_5_out);
endmodule
