// Logisim project flipflop.circ as structural Verilog
module edge_triggered_D_type_flip_flop_w_reset (
  input  Reset,
  input  Data,
  input  Clock,
  output Q,
  output Q_2
);

  wire and_1_out, and_2_out, and_3_out, and_4_out, nor_1_out, nor_2_out, not_1_out, not_2_out, or_1_out;

  not not_1 (not_1_out, Clock);
  not not_2 (not_2_out, Data);
  and and_1 (and_1_out, Data, not_1_out);
  and and_2 (and_2_out, not_1_out, not_2_out);
  nor nor_1 (nor_1_out, and_1_out, nor_2_out);
  nor nor_2 (nor_2_out, nor_1_out, and_2_out);
  or or_1 (or_1_out, Reset, and_3_out);
  and and_3 (and_3_out, nor_1_out, Clock);
  and and_4 (and_4_out, Clock, nor_2_out);
  nor nor_3 (Q, or_1_out, Q_2);
  nor nor_4 (Q_2, Q, and_4_out);
endmodule

module Register (
  input  Reset,
  input  Clock,
  input  [7:0] Input,
  output [7:0] Output
);

  edge_triggered_D_type_flip_flop_w_reset edge_triggered_d_type_flip_flop_w_reset_1 (
    .Reset(Reset), .Data(Input[0]), .Clock(Clock), .Q(Output[0]));  // open: Q_2
  edge_triggered_D_type_flip_flop_w_reset edge_triggered_d_type_flip_flop_w_reset_2 (
    .Reset(Reset), .Data(Input[1]), .Clock(Clock), .Q(Output[1]));  // open: Q_2
  edge_triggered_D_type_flip_flop_w_reset edge_triggered_d_type_flip_flop_w_reset_3 (
    .Reset(Reset), .Data(Input[2]), .Clock(Clock), .Q(Output[2]));  // open: Q_2
  edge_triggered_D_type_flip_flop_w_reset edge_triggered_d_type_flip_flop_w_reset_4 (
    .Reset(Reset), .Data(Input[3]), .Clock(Clock), .Q(Output[3]));  // open: Q_2
  edge_triggered_D_type_flip_flop_w_reset edge_triggered_d_type_flip_flop_w_reset_5 (
    .Reset(Reset), .Data(Input[4]), .Clock(Clock), .Q(Output[4]));  // open: Q_2
  edge_triggered_D_type_flip_flop_w_reset edge_triggered_d_type_flip_flop_w_reset_6 (
    .Reset(Reset), .Data(Input[5]), .Clock(Clock), .Q(Output[5]));  // open: Q_2
  edge_triggered_D_type_flip_flop_w_reset edge_triggered_d_type_flip_flop_w_reset_7 (
    .Reset(Reset), .Data(Input[6]), .Clock(Clock), .Q(Output[6]));  // open: Q_2
  edge_triggered_D_type_flip_flop_w_reset edge_triggered_d_type_flip_flop_w_reset_8 (
    .Reset(Reset), .Data(Input[7]), .Clock(Clock), .Q(Output[7]));  // open: Q_2
endmodule

module Counter (
  input  Reset,
  output [7:0] Output
);

  wire Clock_out;
  wire [7:0] adder_1_out;

  Clock Clock (.out(Clock_out));
  Register register_1 (.Reset(Reset), .Clock(Clock_out), .Input(adder_1_out), .Output(Output));
  Adder adder_1 (.a(Output), .b(8'h1), .out(adder_1_out));  // open: cin, cout
endmodule
