// Logisim project gates.circ as structural Verilog: 1 circuit, main circuit main
module main (
  input  _00___0,
  input  in_2
);

  wire and_1_out, and_2_out, and_3_out, nor_1_out, not_1_out, not_2_out, or_1_out, or_2_out, or_3_out,
       or_4_out, or_5_out, or_6_out, or_7_out;

  _7_Segment_Display u_7_segment_display_1 (
    .g(or_1_out), .f(or_2_out), .a(or_4_out), .b(or_6_out), .e(or_3_out), .d(or_5_out), .c(or_7_out));  // open: dp
  or or_1 (or_1_out, and_2_out, and_3_out);
  buf or_2 (or_2_out, nor_1_out);  // OR_Gate
  or or_3 (or_3_out, nor_1_out, and_2_out);
  or or_4 (or_4_out, nor_1_out, and_2_out, and_3_out);
  or or_5 (or_5_out, nor_1_out, and_2_out, and_3_out);
  or or_6 (or_6_out, nor_1_out, and_1_out, and_2_out, and_3_out);
  or or_7 (or_7_out, nor_1_out, and_1_out, and_3_out);
  nor nor_1 (nor_1_out, _00___0, in_2);
  and and_1 (and_1_out, not_1_out, in_2);
  and and_2 (and_2_out, _00___0, not_2_out);
  and and_3 (and_3_out, _00___0, in_2);
  not not_1 (not_1_out, _00___0);
  not not_2 (not_2_out, in_2);

  // Notes on the sheet:
  //   01 = 1
  //   10 = 2
  //   11 = 3
  //   middle
  //   top left
  //   bottom left
  //   top top
  //   bottom bottom
  //   top right
  //   bottom right
  //   NOR (0)
  //   AND + NOT  (1)
  //   AND + NOT (2)
  //   AND (3)
endmodule
