// Logisim project tictactoe.circ as structural Verilog: 1 circuit, main circuit main
module main (
  input  in_1,
  input  in_2,
  input  in_3,
  input  in_4,
  input  in_5,
  input  in_6,
  input  in_7,
  input  in_8,
  input  in_9
);

  wire and_1_out, and_2_out, and_3_out, and_4_out, and_5_out, and_6_out, and_7_out, and_8_out, and_9_out,
       and_10_out, and_11_out, and_12_out, and_13_out, and_14_out, and_15_out, and_16_out, and_17_out,
       and_18_out, and_19_out, and_20_out, and_21_out, and_22_out, and_23_out, and_24_out, nor_1_out,
       nor_2_out, nor_3_out, nor_4_out, nor_5_out, nor_6_out, nor_7_out, nor_8_out, or_1_out, or_2_out,
       or_3_out, or_4_out, or_5_out, or_6_out, or_7_out, or_8_out, or_9_out, or_10_out, xor_1_out, xor_2_out,
       xor_3_out, xor_4_out, xor_5_out, xor_6_out, xor_7_out, xor_8_out, xor_9_out, xor_10_out, xor_11_out,
       xor_12_out, xor_13_out, xor_14_out, xor_15_out, xor_16_out;

  xor xor_1 (xor_1_out, in_2, in_1);
  and and_1 (and_1_out, in_1, in_2);
  xor xor_2 (xor_2_out, in_5, in_4);
  and and_2 (and_2_out, in_4, in_5);
  xor xor_3 (xor_3_out, in_8, in_7);
  and and_3 (and_3_out, in_7, in_8);
  xor xor_4 (xor_4_out, in_4, in_1);
  and and_4 (and_4_out, in_1, in_4);
  xor xor_5 (xor_5_out, in_5, in_2);
  and and_5 (and_5_out, in_2, in_5);
  xor xor_6 (xor_6_out, in_6, in_3);
  and and_6 (and_6_out, in_3, in_6);
  xor xor_7 (xor_7_out, in_5, in_1);
  and and_7 (and_7_out, in_1, in_5);
  xor xor_8 (xor_8_out, in_5, in_3);
  and and_8 (and_8_out, in_3, in_5);
  LED Player_0_Wins (.in(or_1_out));
  LED Player_1_Wins (.in(or_2_out));
  xor xor_9 (xor_9_out, in_3, xor_1_out);
  and and_9 (and_9_out, xor_1_out, in_3);
  xor xor_10 (xor_10_out, in_6, xor_2_out);
  and and_10 (and_10_out, xor_2_out, in_6);
  xor xor_11 (xor_11_out, in_9, xor_3_out);
  and and_11 (and_11_out, xor_3_out, in_9);
  xor xor_12 (xor_12_out, in_7, xor_4_out);
  and and_12 (and_12_out, xor_4_out, in_7);
  xor xor_13 (xor_13_out, in_8, xor_5_out);
  and and_13 (and_13_out, xor_5_out, in_8);
  xor xor_14 (xor_14_out, in_9, xor_6_out);
  and and_14 (and_14_out, xor_6_out, in_9);
  xor xor_15 (xor_15_out, in_9, xor_7_out);
  and and_15 (and_15_out, xor_7_out, in_9);
  xor xor_16 (xor_16_out, in_7, xor_8_out);
  and and_16 (and_16_out, xor_8_out, in_7);
  or or_1 (or_1_out, nor_8_out, nor_7_out, nor_6_out, nor_5_out, nor_4_out, nor_3_out, nor_2_out, nor_1_out);
  or or_2 (or_2_out, and_24_out, and_23_out, and_22_out, and_21_out, and_20_out, and_19_out, and_18_out, and_17_out);
  and and_17 (and_17_out, xor_9_out, or_3_out);
  or or_3 (or_3_out, and_9_out, and_1_out);
  nor nor_1 (nor_1_out, xor_9_out, or_3_out);
  and and_18 (and_18_out, xor_10_out, or_4_out);
  or or_4 (or_4_out, and_10_out, and_2_out);
  nor nor_2 (nor_2_out, xor_10_out, or_4_out);
  and and_19 (and_19_out, xor_11_out, or_5_out);
  or or_5 (or_5_out, and_11_out, and_3_out);
  nor nor_3 (nor_3_out, xor_11_out, or_5_out);
  and and_20 (and_20_out, xor_12_out, or_6_out);
  or or_6 (or_6_out, and_12_out, and_4_out);
  nor nor_4 (nor_4_out, xor_12_out, or_6_out);
  and and_21 (and_21_out, xor_13_out, or_7_out);
  or or_7 (or_7_out, and_13_out, and_5_out);
  nor nor_5 (nor_5_out, xor_13_out, or_7_out);
  and and_22 (and_22_out, xor_14_out, or_8_out);
  or or_8 (or_8_out, and_14_out, and_6_out);
  nor nor_6 (nor_6_out, xor_14_out, or_8_out);
  and and_23 (and_23_out, xor_15_out, or_9_out);
  or or_9 (or_9_out, and_15_out, and_7_out);
  nor nor_7 (nor_7_out, xor_15_out, or_9_out);
  and and_24 (and_24_out, xor_16_out, or_10_out);
  or or_10 (or_10_out, and_16_out, and_8_out);
  nor nor_8 (nor_8_out, xor_16_out, or_10_out);

  // Notes on the sheet:
  //   TR-BL diag
  //   top hor
  //   middle hor
  //   bot hor
  //   left vert
  //   mid vert
  //   right vert
  //   TL-BR diag
endmodule
